# Fritzing sketch Wifi_Humidity_Sensor (saved by Fritzing 0.9.2b)
breadboards: 1

parts:
  U4 = ESP8266 WiFi Module [part_number=ESP8266]
  U6 = Voltage Regulator [part_number=LD1117D33 package=sot223]
  C7 = Electrolytic Capacitor [capacitance=100µF voltage=16V package="0605 [SMD, electrolytic]"]
  C8 = Electrolytic Capacitor [capacitance=10µF voltage=16V package="0605 [SMD, electrolytic]"]
  R8 = Resistor [tolerance=±5% resistance=18k package="1206 [SMD]"]
  R9 = Resistor [tolerance=±5% resistance=1k package="1206 [SMD]"]
  J4 = Screw terminal - 2 pins [part_number="12V VCC" package=THT]
  JP2 = FTDI_BASIC [package=ftdi_basic]
  J6 = female pin header, 2 pins [form="♀ (female)"]
  RHT1 = Humidity and Temperature Sensor RHT03
  R10 = Resistor [tolerance=±5% resistance=10k package="1206 [SMD]"]

nets:
  N1: U4.RXD, R8.Pin_0, R9.Pin_1
  3.3V: U4.VCC, U4.CH_PD, U6.OUT, C7.+, RHT1.Vcc, R10.Pin_0
  N2: U4.GPIO_0, J6.pin1
  N3: U4.GPIO_2, RHT1.Data-signal, R10.Pin_1
  GND: U4.GND, U6.ADJ, C7.-, C8.-, R8.Pin_1, J4.pin2, JP2.2, J6.pin2, RHT1.GND_2
  N4: U4.TXD, JP2.5
  12V: U6.IN, C8.+, J4.pin1
  N5: R9.Pin_0, JP2.4

custom parts:
  ESP8266 WiFi Module: Generic WiFi Module based on the ESP8266 with onboard PCB antenna and UART communications
