# Fritzing sketch Wifi_PWM (saved by Fritzing 0.9.2b)
circuit board: 3.49779cm x 2.63741cm
breadboards: 1

parts:
  U1 = ESP8266 WiFi Module [part_number=ESP8266]
  J1 = Screw terminal - 2 pins [part_number="12V VCC" package=THT]
  J2 = Screw terminal - 2 pins [part_number="STRIP LED" package=THT]
  JP1 = FTDI_BASIC [package=ftdi_basic]
  J3 = female pin header, 2 pins [form="♀ (female)"]
  Q2 = Basic FET P-Channel [part_number=IRF520 package="TO220 [THT]"]
  U2 = Voltage Regulator [part_number=LD1117D33 package=sot223]
  C1 = Electrolytic Capacitor [capacitance=10µF voltage=16V package="0605 [SMD, electrolytic]"]
  C2 = Electrolytic Capacitor [capacitance=100µF voltage=16V package="0605 [SMD, electrolytic]"]
  C4 = Electrolytic Capacitor [capacitance=100µF voltage=16V package="0605 [SMD, electrolytic]"]
  C3 = Electrolytic Capacitor [capacitance=10µF voltage=16V package="0605 [SMD, electrolytic]"]
  U3 = Voltage Regulator [part_number=LD1117D50 package=sot223]
  R4 = Resistor [tolerance=±5% resistance=10k package="1206 [SMD]"]
  R3 = Resistor [tolerance=±5% resistance=22k package="1206 [SMD]"]
  R2 = Resistor [tolerance=±5% resistance=1k package="1206 [SMD]"]
  Q1 = TRANSISTOR_NPN [package=sot23]
  R1 = Resistor [tolerance=±5% resistance=1k package="1206 [SMD]"]
  R6 = Resistor [tolerance=±5% resistance=1k package="1206 [SMD]"]
  R5 = Resistor [tolerance=±5% resistance=18k package="1206 [SMD]"]
  R7 = Resistor [tolerance=±5% resistance=1k package="1206 [SMD]"]

nets:
  N1: U1.RXD, R6.Pin_1, R5.Pin_0
  3.3V: U1.VCC, U1.CH_PD, U2.OUT, C2.+, R7.Pin_1
  N2: U1.GPIO_0, J3.pin1
  N3: U1.GPIO_2, R1.Pin_0
  GND: U1.GND, J1.pin2, JP1.2, J3.pin2, Q2.source, U2.ADJ, C1.-, C2.-, C4.-, C3.-, U3.ADJ, R3.Pin_1, Q1.E, R5.Pin_1
  N4: U1.TXD, JP1.5
  12V: J1.pin1, J2.pin1, U2.IN, C1.+, C3.+, U3.IN
  N5: J2.pin2, Q2.drain
  N6: JP1.4, R6.Pin_0
  N7: Q2.gate, R4.Pin_1, R3.Pin_0
  5V: C4.+, U3.OUT, R2.Pin_0
  N8: R4.Pin_0, R2.Pin_1, Q1.C
  N9: Q1.B, R1.Pin_1, R7.Pin_0

custom parts:
  ESP8266 WiFi Module: Generic WiFi Module based on the ESP8266 with onboard PCB antenna and UART communications
